// Digital circuit Multiplier_4Bit.dig as structural Verilog
module Multiplier_4Bit (
  input  [3:0] A,
  input  [3:0] B,
  output [7:0] RESULT
);

  wire and_1_out, and_2_out, and_3_out, and_4_out, and_5_out, and_6_out, and_7_out, and_8_out, and_9_out,
       and_10_out, and_11_out, and_12_out, and_13_out, and_14_out, and_15_out, and_16_out;

  and and_1 (and_1_out, A[0], B[0]);
  and and_2 (and_2_out, A[0], B[1]);
  and and_3 (and_3_out, A[0], B[2]);
  and and_4 (and_4_out, A[0], B[3]);
  and and_5 (and_5_out, A[1], B[0]);
  and and_6 (and_6_out, A[1], B[1]);
  and and_7 (and_7_out, A[1], B[2]);
  and and_8 (and_8_out, A[1], B[3]);
  and and_9 (and_9_out, A[2], B[0]);
  and and_10 (and_10_out, A[2], B[1]);
  and and_11 (and_11_out, A[2], B[2]);
  and and_12 (and_12_out, A[2], B[3]);
  and and_13 (and_13_out, A[3], B[0]);
  and and_14 (and_14_out, A[3], B[1]);
  and and_15 (and_15_out, A[3], B[2]);
  and and_16 (and_16_out, A[3], B[3]);

  // Other names for the same wires on the sheet: B3 = B[2]; B4 = B[3]
endmodule
